# Fritzing sketch CNC (saved by Fritzing 0.9.3b)
breadboards: 1

parts:
  Parça1 = Arduino Uno (Rev3)
  M1 = Stepper Motor - Bipolar  # not connected
  M2 = Stepper Motor - Bipolar
  J1 = Basic Servo
  IC1 = L293D [package=THT]
  IC2 = L293D [package=THT]
  VCC1 = 4 x AAA Battery Mount

nets:
  N1: Parça1.D8, IC2.In_1
  N2: Parça1.D9_PWM, IC2.In_2
  N3: Parça1.D10_PWM/SS, IC2.In_3
  N4: Parça1.D11_PWM/MOSI, IC2.In_4
  N5: Parça1.D6_PWM, J1.pulse
  N6: Parça1.5V, IC1.Enable_1, IC2.Enable_1, IC2.Enable_2, IC2.+V
  N7: Parça1.GND, IC2.0V, VCC1.-
  N8: M2.A, IC2.Out_1_(_Controlled_by_Enable_1_)
  N9: M2.C, IC2.Out_2_(_Controlled_by_Enable_1_)
  N10: M2.B, IC2.Out_4_(_Controlled_by_Enable_2_)
  N11: M2.D, IC2.Out_3_(_Controlled_by_Enable_2_)
  N12: IC2.+Vmotor, VCC1.+
